// Logisim project logic_analyzer.circ as structural Verilog: 1 circuit, main circuit main
module main (
  input  s_cmd,
  input  s_clock,
  input  ex_cmd,
  input  not_input_clear,
  input  clear,
  input  Record_Clock,
  input  Record_trigger,
  output out_8,
  output s_read,
  output [3:0] out_10
);

  wire and_1_out, d_ff_1_q, d_ff_2_q, d_ff_2_qn, decoder_1_out0, decoder_1_out1, decoder_1_out2,
       decoder_1_out3, decoder_1_out4, decoder_1_out5, decoder_1_out6, decoder_1_out7, nand_2_out, nor_1_out,
       not_1_out, not_3_out, not_10_out, not_11_out, not_12_out, not_13_out, shift_register_1_out,
       shift_register_1_q0;
  wire [2:0] shift_register_1_q3;
  wire [3:0] counter_1_q, rom_1_data;

  not not_1 (not_1_out, not_3_out);
  Shift_Register #(.length(4)) shift_register_1 (
    .in(s_cmd), .clk(s_clock), .out(shift_register_1_out), .load(not_1_out), .d0(out_10[3]),
    .q0(shift_register_1_q0), .d1(out_10[2]), .q1(shift_register_1_q3[2]), .d2(out_10[1]),
    .q2(shift_register_1_q3[1]), .d3(out_10[0]), .q3(shift_register_1_q3[0]));  // open: shift, clr
  Decoder #(.select(3), .disabled(0)) decoder_1 (
    .out0(decoder_1_out0), .out1(decoder_1_out1), .out2(decoder_1_out2), .out3(decoder_1_out3),
    .out4(decoder_1_out4), .out5(decoder_1_out5), .out6(decoder_1_out6), .out7(decoder_1_out7),
    .sel(shift_register_1_q3), .en(ex_cmd));
  // NOT_Gate not_2 has open pins: in=decoder_1_out3, out=open
  not not_3 (not_3_out, decoder_1_out0);
  // NOT_Gate not_4 has open pins: in=decoder_1_out1, out=open
  // NOT_Gate not_5 has open pins: in=decoder_1_out2, out=open
  // NOT_Gate not_6 has open pins: in=decoder_1_out5, out=open
  // NOT_Gate not_7 has open pins: in=decoder_1_out4, out=open
  buf buffer_1 (s_read, shift_register_1_out);
  // NOT_Gate not_8 has open pins: in=decoder_1_out7, out=open
  // NOT_Gate not_9 has open pins: in=decoder_1_out6, out=open
  nand nand_1 (out_8, d_ff_2_q, Record_Clock);
  and and_1 (and_1_out, shift_register_1_q0, not_10_out);
  not not_10 (not_10_out, d_ff_2_qn);
  D_Flip_Flop d_ff_1 (.clk(Record_trigger), .D(1'b1), .Q(d_ff_1_q), .reset(not_11_out));  // open: Qn, preset, en
  not not_11 (not_11_out, clear);
  ROM #(.addrWidth(4), .dataWidth(4)) rom_1 (.addr(counter_1_q), .data(rom_1_data), .sel(1'b1));
  Counter #(.width(4), .max('hf)) counter_1 (.Q(counter_1_q), .clk(Record_Clock));  // open: load, D, count, carry, clr
  nand nand_2 (nand_2_out, counter_1_q[3], d_ff_1_q);
  not not_12 (not_12_out, and_1_out);
  nor nor_1 (nor_1_out, and_1_out, not_10_out);
  D_Flip_Flop d_ff_2 (
    .clk(nand_2_out), .D(1'b1), .Q(d_ff_2_q), .Qn(d_ff_2_qn), .reset(not_13_out));  // open: preset, en
  not not_13 (not_13_out, clear);
  // NAND_Gate nand_3 is placed but not wired
  RAM #(.addrWidth(4), .dataWidth(4), .bus("separate")) ram_1 (
    .addr(counter_1_q), .din(rom_1_data), .data(out_10), .str(nor_1_out), .sel(not_12_out),
    .clk(Record_Clock), .ld(not_10_out), .clr(not_input_clear));

  // Notes on the sheet:
  //   RAM WE
  //   Ripple Carry out of the 4b counter resets the system.
  //   triggered
  //   contents of rom_1 (hex, n*v repeats v):
  //   5*0 7 7 7 4
  //   PENDING DESIGN CHANGES NOT IN KICAD
endmodule
