// Logisim project motor_controller.circ as structural Verilog: 1 circuit, main circuit main
module main (
  input  direction,
  output out_2,
  output out_3,
  output out_4,
  output out_5
);

  wire clock_1_out, nand_1_out, nand_2_out, nand_3_out, nand_4_out, nand_5_out, nand_6_out, nand_7_out,
       nand_8_out, nand_9_out, nand_10_out, nand_11_out, nand_12_out, nand_13_out;

  nand nand_1 (nand_1_out, out_2, out_5);
  nand nand_2 (nand_2_out, out_2, nand_1_out);
  nand nand_3 (nand_3_out, nand_2_out, nand_4_out);
  nand nand_4 (nand_4_out, nand_1_out, out_5);
  nand nand_5 (nand_5_out, direction, direction);
  nand nand_6 (nand_6_out, nand_5_out, nand_3_out);
  nand nand_7 (nand_7_out, direction, nand_3_out);
  Clock clock_1 (.out(clock_1_out));
  nand nand_8 (nand_8_out, nand_5_out, nand_6_out);
  nand nand_9 (nand_9_out, nand_8_out, nand_10_out);
  nand nand_10 (nand_10_out, nand_6_out, nand_3_out);
  nand nand_11 (nand_11_out, direction, nand_7_out);
  nand nand_12 (nand_12_out, nand_11_out, nand_13_out);
  nand nand_13 (nand_13_out, nand_7_out, nand_3_out);
  J_K_Flip_Flop j_k_ff_1 (
    .J(nand_9_out), .clk(clock_1_out), .K(nand_9_out), .Q(out_2), .Qn(out_3));  // open: preset, en, reset
  J_K_Flip_Flop j_k_ff_2 (
    .J(nand_12_out), .clk(clock_1_out), .K(nand_12_out), .Q(out_4), .Qn(out_5));  // open: preset, en, reset

  // Notes on the sheet:
  //   feedback xor
endmodule
