// Logisim project motor_controller_2.circ as structural Verilog: 1 circuit, main circuit main
module main (
  input  direction,
  output out_2,
  output out_3,
  output out_4,
  output out_5
);

  wire clock_1_out, nand_1_out, nand_2_out, nand_3_out, nand_4_out, nand_5_out, nand_6_out, nand_7_out,
       nand_8_out;

  nand nand_1 (nand_1_out, direction, out_5);
  nand nand_2 (nand_2_out, direction, out_2);
  Clock clock_1 (.out(clock_1_out));
  nand nand_3 (nand_3_out, direction, nand_1_out);
  nand nand_4 (nand_4_out, nand_3_out, nand_5_out);
  nand nand_5 (nand_5_out, nand_1_out, out_5);
  nand nand_6 (nand_6_out, direction, nand_2_out);
  nand nand_7 (nand_7_out, nand_6_out, nand_8_out);
  nand nand_8 (nand_8_out, nand_2_out, out_2);
  D_Flip_Flop d_ff_1 (.clk(clock_1_out), .D(nand_4_out), .Q(out_2), .Qn(out_3));  // open: preset, en, reset
  D_Flip_Flop d_ff_2 (.clk(clock_1_out), .D(nand_7_out), .Q(out_4), .Qn(out_5));  // open: preset, en, reset
endmodule
