// Logisim project 25aa1024 circuit.circ as structural Verilog: 1 circuit, main circuit main
module main (
  input  in_1,
  input  [15:0] in_2
);

  wire clock_1_out, multiplexer_1_out, multiplexer_2_out, multiplexer_3_out, multiplexer_4_out,
       multiplexer_5_out, nand_1_out, not_1_out, not_2_out, shift_register_1_out, shift_register_2_out,
       shift_register_3_out;
  wire [1:0] counter_1_q_2;
  wire [7:0] counter_1_q;

  Counter counter_1 (
    .Q({counter_1_q[7:4], counter_1_q_2, counter_1_q[1:0]}), .clk(clock_1_out), .clr(in_1));  // open: load, D, count, carry
  Clock clock_1 (.out(clock_1_out));
  Multiplexer #(.select(2), .enable("false")) multiplexer_1 (
    .in0(in_2[0]), .in1(in_2[1]), .in2(in_2[2]), .in3(in_2[3]), .out(multiplexer_1_out),
    .sel(counter_1_q[1:0]));
  Multiplexer #(.select(2), .enable("false")) multiplexer_2 (
    .in0(in_2[4]), .in1(in_2[5]), .in2(in_2[6]), .in3(in_2[7]), .out(multiplexer_2_out),
    .sel(counter_1_q[1:0]));
  Multiplexer #(.select(2), .enable("false")) multiplexer_3 (
    .in0(in_2[8]), .in1(in_2[9]), .in2(in_2[10]), .in3(in_2[11]), .out(multiplexer_3_out),
    .sel(counter_1_q[1:0]));
  Multiplexer #(.select(2), .enable("false")) multiplexer_4 (
    .in0(in_2[12]), .in1(in_2[13]), .in2(in_2[14]), .in3(in_2[15]), .out(multiplexer_4_out),
    .sel(counter_1_q[1:0]));
  nand nand_1 (nand_1_out, counter_1_q[1], counter_1_q_2[0], ~counter_1_q_2[1]);  // NAND_Gate
  not not_1 (not_1_out, counter_1_q[4]);
  // NAND_Gate nand_2 has open pins: in0=counter_1_q[1], in1=counter_1_q_2[0], in2=counter_1_q_2[1], out=open
  Multiplexer #(.select(2)) multiplexer_5 (
    .in0(multiplexer_1_out), .in1(multiplexer_2_out), .in2(multiplexer_3_out), .in3(multiplexer_4_out),
    .out(multiplexer_5_out), .sel(counter_1_q_2), .en(not_2_out));
  not not_2 (not_2_out, not_1_out);
  assign multiplexer_5_out = not_1_out ? nand_1_out : 1'bz;  // Controlled_Buffer controlled_buffer_1
  Shift_Register shift_register_1 (
    .in(multiplexer_5_out), .clk(clock_1_out), .out(shift_register_1_out), .clr(in_1));  // open: shift, load, d0, q0, d1, q1, d2, q2, d3, q3, d4, q4, d5, q5, d6, q6, d7, q7
  Shift_Register shift_register_2 (
    .in(shift_register_3_out), .clk(clock_1_out), .out(shift_register_2_out), .clr(in_1));  // open: shift, load, d0, q0, d1, q1, d2, q2, d3, q3, d4, q4, d5, q5, d6, q6, d7, q7
  Shift_Register shift_register_3 (
    .in(shift_register_1_out), .clk(clock_1_out), .out(shift_register_3_out), .clr(in_1));  // open: shift, load, d0, q0, d1, q1, d2, q2, d3, q3, d4, q4, d5, q5, d6, q6, d7, q7
  Shift_Register shift_register_4 (
    .in(shift_register_2_out), .clk(clock_1_out), .clr(in_1));  // open: shift, out, load, d0, q0, d1, q1, d2, q2, d3, q3, d4, q4, d5, q5, d6, q6, d7, q7
endmodule
