// Logisim project 25aa1024_shift_registers.circ as structural Verilog
module main (
);

  wire clock_1_out, shift_register_1_out, shift_register_2_out, shift_register_3_out, shift_register_4_out,
       shift_register_5_out, shift_register_6_out, shift_register_7_out;
  wire [7:0] shift_register_2_q7, shift_register_4_q7, shift_register_8_q7;
  wire [16:16] shift_register_6_q0;

  Shift_Register shift_register_1 (
    .clk(clock_1_out), .out(shift_register_1_out));  // open: shift, in, load, clr, d0, q0, d1, q1, d2, q2, d3, q3, d4, q4, d5, q5, d6, q6, d7, q7
  Clock clock_1 (.out(clock_1_out));
  Shift_Register shift_register_2 (
    .in(shift_register_7_out), .clk(clock_1_out), .out(shift_register_2_out), .q0(shift_register_2_q7[7]),
    .q1(shift_register_2_q7[6]), .q2(shift_register_2_q7[5]), .q3(shift_register_2_q7[4]),
    .q4(shift_register_2_q7[3]), .q5(shift_register_2_q7[2]), .q6(shift_register_2_q7[1]),
    .q7(shift_register_2_q7[0]));  // open: shift, load, clr, d0, d1, d2, d3, d4, d5, d6, d7
  Shift_Register shift_register_3 (
    .in(shift_register_1_out), .clk(clock_1_out), .out(shift_register_3_out));  // open: shift, load, clr, d0, q0, d1, q1, d2, q2, d3, q3, d4, q4, d5, q5, d6, q6, d7, q7
  Shift_Register shift_register_4 (
    .in(shift_register_2_out), .clk(clock_1_out), .out(shift_register_4_out), .q0(shift_register_4_q7[7]),
    .q1(shift_register_4_q7[6]), .q2(shift_register_4_q7[5]), .q3(shift_register_4_q7[4]),
    .q4(shift_register_4_q7[3]), .q5(shift_register_4_q7[2]), .q6(shift_register_4_q7[1]),
    .q7(shift_register_4_q7[0]));  // open: shift, load, clr, d0, d1, d2, d3, d4, d5, d6, d7
  Shift_Register shift_register_5 (
    .in(shift_register_3_out), .clk(clock_1_out), .out(shift_register_5_out));  // open: shift, load, clr, d0, q0, d1, q1, d2, q2, d3, q3, d4, q4, d5, q5, d6, q6, d7, q7
  Shift_Register shift_register_6 (
    .in(shift_register_4_out), .clk(clock_1_out), .out(shift_register_6_out), .q0(shift_register_6_q0[16]));  // open: shift, load, clr, d0, d1, q1, d2, q2, d3, q3, d4, q4, d5, q5, d6, q6, d7, q7
  Shift_Register shift_register_7 (
    .in(shift_register_5_out), .clk(clock_1_out), .out(shift_register_7_out));  // open: shift, load, clr, d0, q0, d1, q1, d2, q2, d3, q3, d4, q4, d5, q5, d6, q6, d7, q7
  Shift_Register shift_register_8 (
    .in(shift_register_6_out), .clk(clock_1_out), .q0(shift_register_8_q7[7]), .q1(shift_register_8_q7[6]),
    .q2(shift_register_8_q7[5]), .q3(shift_register_8_q7[4]), .q4(shift_register_8_q7[3]),
    .q5(shift_register_8_q7[2]), .q6(shift_register_8_q7[1]), .q7(shift_register_8_q7[0]));  // open: shift, out, load, clr, d0, d1, d2, d3, d4, d5, d6, d7
  ROM #(.addrWidth(17)) rom_1 (.addr({shift_register_6_q0[16], shift_register_4_q7, shift_register_2_q7}));  // open: data, sel
endmodule

module instr_mem_ctrl (
  input  reset_n,
  input  next_instr,
  output CS,
  output [5:0] addr
);

  wire not_1_out;

  not not_1 (not_1_out, reset_n);
  Counter #(.width(6), .max('h3f)) counter_1 (
    .load(1'b0), .D({6{1'b0}}), .count(1'b1), .Q(addr), .clk(next_instr), .clr(not_1_out));  // open: carry

  assign CS = reset_n;
endmodule
