// Digital circuit plc.dig as structural Verilog
module plc (
);

  wire _74153_1_pin7, _74153_1_pin9, _74153_2_pin7, _74153_2_pin9;

  _74153 _74153_1 (
    .pin1(1'b0), .pin7(_74153_1_pin7), .pin8(1'b0), .pin9(_74153_1_pin9), .pin15(1'b0), .pin16(1'b1));  // open: pin2, pin3, pin4, pin5, pin6, pin10, pin11, pin12, pin13, pin14
  _74153 _74153_2 (
    .pin1(1'b0), .pin7(_74153_2_pin7), .pin8(1'b0), .pin9(_74153_2_pin9), .pin15(1'b0), .pin16(1'b1));  // open: pin2, pin3, pin4, pin5, pin6, pin10, pin11, pin12, pin13, pin14
  _7485 _7485_1 (
    .pin8(1'b0), .pin10(_74153_1_pin7), .pin12(_74153_1_pin9), .pin13(_74153_2_pin7), .pin15(_74153_2_pin9),
    .pin16(1'b1));  // open: pin1, pin2, pin3, pin4, pin5, pin6, pin7, pin9, pin11, pin14
endmodule
