// Digital circuit addr_decoder_74153.dig as structural Verilog
module addr_decoder_74153 (
  input  clk,
  input  nrst,
  input  nint,
  input  VCC_5V,
  input  GND,
  input  VCC_3V3,
  input  we,
  input  oe,
  input  [7:0] data,
  input  [15:0] addr,
  input  [7:0] aux_bus
);

  wire _74153_1_pin7, _74153_1_pin9;

  _74153 _74153_1 (
    .pin1(addr[15]), .pin2(addr[13]), .pin3(we), .pin4(1'b0), .pin5(1'b0), .pin6(1'b0), .pin7(_74153_1_pin7),
    .pin8(1'b0), .pin9(_74153_1_pin9), .pin10(1'b0), .pin11(1'b0), .pin12(1'b0), .pin13(oe),
    .pin14(addr[12]), .pin15(addr[14]), .pin16(1'b1));

  // Notes on the sheet:
  //   nrst: default 1
  //   nint: default 1
  //   VCC_5V: default 1
  //   VCC_3V3: default 1
endmodule
