// Digital circuit addr_decoder_7bits_rdonly.dig as structural Verilog
module addr_decoder_7bits_rdonly (
  input  clk,
  input  nrst,
  input  nint,
  input  VCC_5V,
  input  GND,
  input  VCC_3V3,
  input  we,
  input  oe,
  input  [7:0] data,
  input  [15:0] addr,
  input  [7:0] aux_bus,
  output nwe
);

  wire not_1_out, not_2_out;

  not not_1 (not_1_out, addr[15]);
  not not_2 (not_2_out, addr[10]);
  nand nand_1 (nwe, we, not_1_out, addr[14], addr[13], addr[12], addr[11], not_2_out, addr[9]);

  // Notes on the sheet:
  //   nrst: default 1
  //   nint: default 1
  //   VCC_5V: default 1
  //   VCC_3V3: default 1
endmodule
