// Digital circuit addr_decoder_8bits_rw.dig as structural Verilog
module addr_decoder_8bits_rw (
  input  clk,
  input  nrst,
  input  nint,
  input  VCC_5V,
  input  GND,
  input  VCC_3V3,
  input  we,
  input  oe,
  input  [7:0] data,
  input  [15:0] addr,
  input  [7:0] aux_bus
);

  wire nand_1_out, not_1_out, or_1_out, or_2_out;

  not not_1 (not_1_out, addr[14]);
  nand nand_1 (nand_1_out, addr[15], addr[13], addr[12], addr[11], addr[10], addr[9], addr[8]);  // open: In_2
  or or_1 (or_1_out, we, nand_1_out);
  or or_2 (or_2_out, oe, nand_1_out);

  // Notes on the sheet:
  //   nrst: default 1
  //   nint: default 1
  //   VCC_5V: default 1
  //   VCC_3V3: default 1
endmodule
