// Digital circuit w_74161.dig as structural Verilog
module w_74161 (
  input  clk,
  input  nrst,
  input  en,
  input  cin,
  input  [3:0] din,
  input  nld,
  output [3:0] dout,
  output cout
);

  _74161 _74161_1 (
    .pin1(nrst), .pin2(clk), .pin3(din[0]), .pin4(din[1]), .pin5(din[2]), .pin6(din[3]), .pin7(en),
    .pin8(1'b0), .pin9(nld), .pin10(cin), .pin11(dout[3]), .pin12(dout[2]), .pin13(dout[1]), .pin14(dout[0]),
    .pin15(cout), .pin16(1'b1));

  // Notes on the sheet:
  //   nrst: default 1
  //   en: default 1
  //   cin: default 1
  //   nld: default 1
endmodule
