// Digital circuit dumb_op_card.dig as structural Verilog
module dumb_op_card (
  input  clk,
  input  nrst,
  input  nint,
  input  VCC_5V,
  input  GND,
  input  VCC_3V3,
  input  nwe,
  input  noe,
  input  [15:0] addr,
  input  [7:0] aux_bus,
  output [7:0] data
);

  wire [3:0] _7404_1_pin2;

  _7404 _7404_1 (
    .pin1(addr[0]), .pin2(_7404_1_pin2[0]), .pin3(addr[1]), .pin4(_7404_1_pin2[1]), .pin5(addr[2]),
    .pin6(_7404_1_pin2[2]), .pin7(1'b0), .pin8(_7404_1_pin2[3]), .pin9(addr[3]), .pin11(1'b0), .pin13(1'b0),
    .pin14(1'b1));  // open: pin10, pin12
  w_74161 w_74161_1 (.clk(clk), .nrst(nrst), .en(1'b1), .cin(1'b1), .din(_7404_1_pin2), .nld(nwe));  // open: dout, cout

  assign data[3:0] = data[7:4];

  // Notes on the sheet:
  //   nrst: default 1
  //   nint: default 1
  //   VCC_5V: default 1
  //   VCC_3V3: default 1
  //   nwe: default 1
  //   noe: default 1
  //   addr: default 5
endmodule
