// Digital circuit led_card.dig as structural Verilog
module led_card (
  input  nrst,
  input  nint,
  input  VCC_5V,
  input  GND,
  input  VCC_3V3,
  input  we,
  input  oe,
  input  [7:0] data,
  input  [15:0] addr,
  input  [7:0] aux_bus,
  input  clk
);

  wire _74138_1_pin7, _74138_1_pin9, _74138_1_pin10, _74138_1_pin11, _74138_1_pin12, _74138_1_pin13,
       _74138_1_pin14, _74138_1_pin15, _74138_2_pin7, _74138_2_pin9, _74138_2_pin10, _74138_2_pin11,
       _74138_2_pin12, _74138_2_pin13, _74138_2_pin14, _74138_2_pin15, not_1_out;
  wire [3:0] _74161_1_pin14, _74189_1_pin5, _74189_2_pin5, multiplexer_1_out;

  not not_1 (not_1_out, we);
  Multiplexer #(.Bits(4)) multiplexer_1 (.sel(not_1_out), .in_0(addr[3:0]), .in_1(4'b0000), .out(multiplexer_1_out));
  _74161 _74161_1 (
    .pin1(1'b1), .pin2(clk), .pin3(1'b0), .pin4(1'b0), .pin5(1'b0), .pin6(1'b0), .pin7(1'b1), .pin8(1'b0),
    .pin9(1'b1), .pin10(1'b1), .pin11(_74161_1_pin14[3]), .pin12(_74161_1_pin14[2]),
    .pin13(_74161_1_pin14[1]), .pin14(_74161_1_pin14[0]), .pin16(1'b1));  // open: pin15
  _74189 _74189_1 (
    .pin1(multiplexer_1_out[0]), .pin2(1'b0), .pin3(not_1_out), .pin4(data[0]), .pin5(_74189_1_pin5[3]),
    .pin6(data[1]), .pin7(_74189_1_pin5[2]), .pin8(1'b0), .pin9(_74189_1_pin5[1]), .pin10(data[2]),
    .pin11(_74189_1_pin5[0]), .pin12(data[3]), .pin13(multiplexer_1_out[3]), .pin14(multiplexer_1_out[2]),
    .pin15(multiplexer_1_out[1]), .pin16(1'b1));
  _74189 _74189_2 (
    .pin1(multiplexer_1_out[0]), .pin2(1'b0), .pin3(not_1_out), .pin4(data[4]), .pin5(_74189_2_pin5[3]),
    .pin6(data[5]), .pin7(_74189_2_pin5[2]), .pin8(1'b0), .pin9(_74189_2_pin5[1]), .pin10(data[6]),
    .pin11(_74189_2_pin5[0]), .pin12(data[7]), .pin13(multiplexer_1_out[3]), .pin14(multiplexer_1_out[2]),
    .pin15(multiplexer_1_out[1]), .pin16(1'b1));
  _74138 _74138_1 (
    .pin1(_74161_1_pin14[0]), .pin2(_74161_1_pin14[1]), .pin3(_74161_1_pin14[2]), .pin4(1'b0), .pin5(1'b0),
    .pin6(_74161_1_pin14[3]), .pin7(_74138_1_pin7), .pin8(1'b0), .pin9(_74138_1_pin9),
    .pin10(_74138_1_pin10), .pin11(_74138_1_pin11), .pin12(_74138_1_pin12), .pin13(_74138_1_pin13),
    .pin14(_74138_1_pin14), .pin15(_74138_1_pin15), .pin16(1'b1));
  _74138 _74138_2 (
    .pin1(_74161_1_pin14[0]), .pin2(_74161_1_pin14[1]), .pin3(_74161_1_pin14[2]), .pin4(1'b0),
    .pin5(_74161_1_pin14[3]), .pin6(1'b1), .pin7(_74138_2_pin7), .pin8(1'b0), .pin9(_74138_2_pin9),
    .pin10(_74138_2_pin10), .pin11(_74138_2_pin11), .pin12(_74138_2_pin12), .pin13(_74138_2_pin13),
    .pin14(_74138_2_pin14), .pin15(_74138_2_pin15), .pin16(1'b1));

  // Notes on the sheet:
  //   nrst: default 1
  //   nint: default 1
  //   VCC_5V: default 1
  //   VCC_3V3: default 1
  //   addr: default 7
  //   clk: Hz: 3
endmodule
