// Logisim project bldc driver.circ as structural Verilog: 2 circuits, main circuit main
module main (
  input  in_1,
  input  in_2,
  input  in_3,
  output A,
  output A_sh_n,
  output B,
  output B_sh_n,
  output C,
  output C_sh_n
);

  wire and_1_out, decoder_1_out0, decoder_1_out1, decoder_1_out2, decoder_1_out3, decoder_1_out4,
       decoder_1_out5, decoder_1_out6, decoder_1_out7, not_1_out, not_2_out, not_3_out, not_4_out, not_5_out,
       not_6_out, not_7_out, not_8_out, or_1_out, or_2_out, or_3_out, xor_1_out;
  wire [2:0] controlled_buffer_1_out, counter_1_q;

  assign controlled_buffer_1_out = in_1 ? 3'b101 : 3'bz;  // Controlled_Buffer controlled_buffer_1
  Pull_Resistor pull_resistor_1 (.node(controlled_buffer_1_out));
  and and_1 (and_1_out, or_1_out, or_3_out);
  or or_1 (or_1_out, in_1, not_8_out);
  not not_1 (not_1_out, in_1);
  // NAND_Gate nand_1 is placed but not wired
  xor xor_1 (xor_1_out, in_1, not_2_out);
  not not_2 (not_2_out, and_1_out);
  or or_2 (or_2_out, and_1_out, in_1);
  or or_3 (or_3_out, not_1_out, not_3_out);
  Counter #(.width(3), .max('h7)) counter_1 (
    .load(xor_1_out), .D(controlled_buffer_1_out), .count(or_2_out), .Q(counter_1_q), .clk(in_2), .clr(in_3));  // open: carry
  not not_3 (not_3_out, decoder_1_out0);
  not not_4 (not_4_out, decoder_1_out1);
  not not_5 (not_5_out, decoder_1_out2);
  not not_6 (not_6_out, decoder_1_out3);
  not not_7 (not_7_out, decoder_1_out4);
  not not_8 (not_8_out, decoder_1_out5);
  // NOT_Gate not_9 has open pins: in=decoder_1_out6, out=open
  // NOT_Gate not_10 has open pins: in=decoder_1_out7, out=open
  Decoder #(.select(3), .disabled(0)) decoder_1 (
    .out0(decoder_1_out0), .out1(decoder_1_out1), .out2(decoder_1_out2), .out3(decoder_1_out3),
    .out4(decoder_1_out4), .out5(decoder_1_out5), .out6(decoder_1_out6), .out7(decoder_1_out7),
    .sel(counter_1_q));  // open: en
  and and_2 (A_sh_n, not_5_out, not_8_out);
  and and_3 (B_sh_n, not_4_out, not_7_out);
  and and_4 (C_sh_n, not_8_out, not_6_out);
  nand nand_2 (A, not_3_out, not_4_out);
  nand nand_3 (B, not_6_out, not_5_out);
  nand nand_4 (C, not_7_out, not_8_out);

  // Notes on the sheet:
  //   74ls138
endmodule

module guh (
  input  in_1,
  input  in_2
);

  wire d_ff_1_q, d_ff_2_q, d_ff_3_q, d_ff_4_q, d_ff_5_q, d_ff_6_q, or_1_out, or_2_out, or_3_out, or_4_out,
       or_5_out, or_6_out, xor_1_out, xor_2_out, xor_3_out, xor_4_out, xor_5_out, xor_6_out;
  wire [2:0] counter_1_q;

  Counter #(.width(3), .max('h7)) counter_1 (.Q(counter_1_q), .clk(in_1), .clr(in_2));  // open: load, D, count, carry
  or or_1 (or_1_out, counter_1_q[1], counter_1_q[0]);
  xor xor_1 (xor_1_out, or_1_out, d_ff_1_q);
  or or_2 (or_2_out, counter_1_q[2], counter_1_q[1]);
  xor xor_2 (xor_2_out, or_2_out, d_ff_2_q);
  or or_3 (or_3_out, counter_1_q[0], counter_1_q[2]);
  xor xor_3 (xor_3_out, or_3_out, d_ff_3_q);
  or or_4 (or_4_out, counter_1_q[1], counter_1_q[0]);
  xor xor_4 (xor_4_out, or_4_out, d_ff_4_q);
  or or_5 (or_5_out, counter_1_q[2], counter_1_q[1]);
  xor xor_5 (xor_5_out, or_5_out, d_ff_5_q);
  or or_6 (or_6_out, counter_1_q[0], counter_1_q[2]);
  xor xor_6 (xor_6_out, or_6_out, d_ff_6_q);
  D_Flip_Flop d_ff_1 (.clk(in_1), .D(xor_1_out), .Q(d_ff_1_q), .preset(in_2));  // open: Qn, en, reset
  D_Flip_Flop d_ff_2 (.clk(in_1), .D(xor_2_out), .Q(d_ff_2_q), .reset(in_2));  // open: Qn, preset, en
  D_Flip_Flop d_ff_3 (.clk(in_1), .D(xor_3_out), .Q(d_ff_3_q), .preset(in_2));  // open: Qn, en, reset
  D_Flip_Flop d_ff_4 (.clk(in_1), .D(xor_4_out), .Q(d_ff_4_q), .preset(in_2));  // open: Qn, en, reset
  D_Flip_Flop d_ff_5 (.clk(in_1), .D(xor_5_out), .Q(d_ff_5_q), .preset(in_2));  // open: Qn, en, reset
  D_Flip_Flop d_ff_6 (.clk(in_1), .D(xor_6_out), .Q(d_ff_6_q), .reset(in_2));  // open: Qn, preset, en
endmodule
