// Logisim project logiim.circ as structural Verilog: 1 circuit, main circuit main
module main (
  input  in_1,
  input  in_2,
  input  in_3,
  input  in_4,
  output [15:0] out_5,
  output [7:0] out_6
);

  wire and_1_out, and_2_out, clock_1_out, decoder_1_out0, decoder_1_out1, decoder_1_out2, decoder_1_out3,
       decoder_1_out4, decoder_1_out5, decoder_1_out6, decoder_1_out7, decoder_1_out8, decoder_1_out9,
       decoder_1_out10, decoder_1_out11, decoder_1_out12, decoder_1_out13, decoder_1_out14, decoder_1_out15,
       decoder_2_out0, decoder_2_out1, decoder_2_out2, decoder_2_out3, decoder_2_out4, decoder_2_out5,
       decoder_2_out6, decoder_2_out7, decoder_2_out8, decoder_2_out9, decoder_2_out10, decoder_2_out11,
       decoder_2_out12, decoder_2_out13, decoder_2_out14, decoder_2_out15, nand_2_out, not_1_out, not_2_out,
       not_3_out, not_4_out, not_5_out, not_6_out, not_7_out, not_8_out, not_9_out, not_10_out, not_11_out,
       not_12_out, not_13_out, not_14_out, not_15_out, not_16_out, not_17_out, not_18_out, not_19_out,
       not_20_out, not_21_out, not_22_out, not_23_out, not_24_out, not_25_out, not_26_out, not_27_out,
       not_28_out, not_29_out, not_30_out, not_31_out, not_32_out, not_33_out, not_34_out, not_35_out,
       not_36_out, not_37_out, not_38_out, not_39_out, not_40_out, not_41_out, not_42_out, not_43_out,
       not_44_out, not_45_out, not_46_out, not_47_out, not_48_out, not_49_out, not_50_out, not_51_out,
       not_52_out, not_53_out, or_1_out, or_2_out, or_3_out, undriven, undriven_2, undriven_3, undriven_4,
       undriven_5;
  wire [7:0] adder_1_out, controlled_buffer_1_out, controlled_buffer_2_out, nand_1_out, register_1_q,
       register_3_q, register_4_q, register_5_q, register_6_q, register_8_q, register_9_q;
  wire [15:0] counter_1_q;
  wire [15:8] register_2_q;

  not not_1 (not_1_out, undriven);
  Register register_1 (.D(out_6), .Q(register_1_q), .clk(undriven_4), .clr(not_3_out));  // open: en
  Register register_2 (.D(out_6), .Q(register_2_q), .clk(undriven_2), .clr(not_2_out));  // open: en
  not not_2 (not_2_out, in_1);
  not not_3 (not_3_out, in_1);
  Register register_3 (.D(out_6), .Q(register_3_q), .clk(undriven_5), .clr(not_5_out));  // open: en
  Register register_4 (.D(out_6), .Q(register_4_q), .clk(undriven_3), .clr(not_4_out));  // open: en
  not not_4 (not_4_out, in_1);
  not not_5 (not_5_out, in_1);
  Adder adder_1 (.a(register_4_q), .b(register_3_q), .out(adder_1_out));  // open: cin, cout
  Counter #(.width(16), .max('hffff)) counter_1 (
    .load(not_1_out), .D({register_2_q, register_1_q}), .Q(counter_1_q), .clk(clock_1_out), .clr(not_6_out));  // open: count, carry
  not not_6 (not_6_out, in_1);
  Clock clock_1 (.out(clock_1_out));
  assign controlled_buffer_1_out = not_7_out ? adder_1_out : 8'bz;  // Controlled_Buffer controlled_buffer_1
  // NOT_Gate not_7 has open pins: in=open, out=not_7_out
  assign controlled_buffer_2_out = not_8_out ? nand_1_out : 8'bz;  // Controlled_Buffer controlled_buffer_2
  // NOT_Gate not_8 has open pins: in=open, out=not_8_out
  assign nand_1_out = ~(register_4_q & register_3_q);  // NAND_Gate nand_1, 8 bits wide
  not not_9 (not_9_out, counter_1_q[1]);
  not not_10 (not_10_out, counter_1_q[0]);
  not not_11 (not_11_out, counter_1_q[0]);
  or or_1 (or_1_out, not_11_out, counter_1_q[1]);
  not not_12 (not_12_out, clock_1_out);
  Controlled_Buffer #(.width(8)) controlled_buffer_3 (.in(register_5_q), .en(not_13_out));  // open: out
  // NOT_Gate not_13 has open pins: in=open, out=not_13_out
  Register register_5 (.D(out_6), .Q(register_5_q), .clr(not_14_out));  // open: en, clk
  Register register_6 (.D(out_6), .Q(register_6_q), .clr(not_15_out));  // open: en, clk
  not not_14 (not_14_out, in_1);
  not not_15 (not_15_out, in_1);
  or or_2 (or_2_out, not_9_out, not_10_out);
  ROM #(.addrWidth(15)) rom_1 (.addr(counter_1_q[15:1]), .data(out_5[7:0]));  // open: sel
  Register register_7 (.D(out_5[7:0]), .Q(out_5[15:8]), .clk(or_3_out));  // open: en, clr
  or or_3 (or_3_out, or_1_out, not_12_out);
  Comparator comparator_1 (.a(register_6_q), .b(register_5_q));  // open: gt, eq, lt
  Comparator comparator_2 (.a(register_5_q), .b({8{1'b1}}));  // open: gt, eq, lt
  not not_16 (not_16_out, out_5[12]);
  Register register_8 (.D(out_6), .Q(register_8_q), .clr(not_17_out));  // open: en, clk
  Register register_9 (.D(out_6), .Q(register_9_q), .clr(not_18_out));  // open: en, clk
  not not_17 (not_17_out, in_1);
  not not_18 (not_18_out, in_1);
  assign out_6 = not_16_out ? out_5[7:0] : 8'bz;  // Controlled_Buffer controlled_buffer_4
  not not_19 (not_19_out, in_2);
  and and_1 (and_1_out, ~or_2_out, clock_1_out);  // AND_Gate
  Decoder #(.select(4), .disabled(0)) decoder_1 (
    .out0(decoder_1_out0), .out1(decoder_1_out1), .out2(decoder_1_out2), .out3(decoder_1_out3),
    .out4(decoder_1_out4), .out5(decoder_1_out5), .out6(decoder_1_out6), .out7(decoder_1_out7),
    .out8(decoder_1_out8), .out9(decoder_1_out9), .out10(decoder_1_out10), .out11(decoder_1_out11),
    .out12(decoder_1_out12), .out13(decoder_1_out13), .out14(decoder_1_out14), .out15(decoder_1_out15),
    .sel(out_5[11:8]), .en(and_1_out));
  not not_20 (not_20_out, clock_1_out);
  Decoder #(.select(4), .disabled(0)) decoder_2 (
    .out0(decoder_2_out0), .out1(decoder_2_out1), .out2(decoder_2_out2), .out3(decoder_2_out3),
    .out4(decoder_2_out4), .out5(decoder_2_out5), .out6(decoder_2_out6), .out7(decoder_2_out7),
    .out8(decoder_2_out8), .out9(decoder_2_out9), .out10(decoder_2_out10), .out11(decoder_2_out11),
    .out12(decoder_2_out12), .out13(decoder_2_out13), .out14(decoder_2_out14), .out15(decoder_2_out15),
    .sel(out_5[7:4]), .en(and_2_out));
  and and_2 (and_2_out, ~or_2_out, ~not_20_out);  // AND_Gate
  RAM #(.addrWidth(16), .bus("asynch")) ram_1 (
    .addr({register_8_q, register_9_q}), .data(out_6), .sel(not_19_out), .ld(nand_2_out));  // open: clr
  nand nand_2 (nand_2_out, not_21_out, in_4);
  not not_21 (not_21_out, in_3);
  not not_22 (not_22_out, decoder_1_out0);
  not not_23 (not_23_out, decoder_1_out1);
  not not_24 (not_24_out, decoder_1_out2);
  not not_25 (not_25_out, decoder_1_out3);
  not not_26 (not_26_out, decoder_1_out4);
  not not_27 (not_27_out, decoder_1_out5);
  not not_28 (not_28_out, decoder_1_out6);
  not not_29 (not_29_out, decoder_1_out7);
  not not_30 (not_30_out, decoder_1_out8);
  not not_31 (not_31_out, decoder_1_out9);
  not not_32 (not_32_out, decoder_1_out10);
  not not_33 (not_33_out, decoder_1_out11);
  not not_34 (not_34_out, decoder_1_out12);
  not not_35 (not_35_out, decoder_1_out13);
  not not_36 (not_36_out, decoder_1_out14);
  not not_37 (not_37_out, decoder_1_out15);
  not not_38 (not_38_out, decoder_2_out0);
  not not_39 (not_39_out, decoder_2_out1);
  not not_40 (not_40_out, decoder_2_out2);
  not not_41 (not_41_out, decoder_2_out3);
  not not_42 (not_42_out, decoder_2_out4);
  not not_43 (not_43_out, decoder_2_out5);
  not not_44 (not_44_out, decoder_2_out6);
  not not_45 (not_45_out, decoder_2_out7);
  not not_46 (not_46_out, decoder_2_out8);
  not not_47 (not_47_out, decoder_2_out9);
  not not_48 (not_48_out, decoder_2_out10);
  not not_49 (not_49_out, decoder_2_out11);
  not not_50 (not_50_out, decoder_2_out12);
  not not_51 (not_51_out, decoder_2_out13);
  not not_52 (not_52_out, decoder_2_out14);
  not not_53 (not_53_out, decoder_2_out15);

  // Notes on the sheet:
  //   contents of rom_1 (hex, n*v repeats v):
  //   f0 0 e7 aa 3
endmodule
