// Logisim project revision_3.circ as structural Verilog: 1 circuit, main circuit main
module main (
  input  CLEAR,
  input  [2:0] EXTFLAGS,
  input  [7:0] in_3,
  output [7:0] EXT_FLAGS,
  output [7:0] out_5,
  output [7:0] EXTDATA
);

  wire adder_1_cout, and_1_out, and_2_out, and_3_out, clock_1_out, comparator_1_eq, decoder_1_out0,
       decoder_1_out1, decoder_1_out2, decoder_1_out3, decoder_1_out4, decoder_1_out5, decoder_1_out6,
       decoder_1_out7, decoder_2_out0, decoder_2_out1, decoder_2_out2, decoder_2_out3, decoder_2_out4,
       decoder_2_out5, decoder_2_out6, decoder_2_out7, decoder_3_out0, decoder_3_out1, decoder_3_out2,
       decoder_3_out3, decoder_3_out4, decoder_3_out5, decoder_3_out6, decoder_3_out7, decoder_4_out0,
       decoder_4_out1, decoder_4_out2, decoder_4_out3, decoder_4_out4, decoder_4_out5, decoder_4_out6,
       decoder_4_out7, decoder_4_out8, decoder_4_out9, decoder_4_out10, decoder_4_out11, decoder_4_out12,
       decoder_4_out13, decoder_4_out14, decoder_4_out15, decoder_5_out0, decoder_5_out1, decoder_5_out2,
       decoder_5_out3, decoder_5_out4, decoder_5_out5, decoder_5_out6, decoder_5_out7, nand_1_out,
       nand_2_out, nand_4_out, nand_5_out, nor_1_out, not_1_out, not_2_out, not_3_out, not_4_out, not_5_out,
       not_6_out, not_7_out, not_15_out, not_16_out, not_17_out, not_18_out, not_19_out, not_20_out,
       not_21_out, not_22_out, not_23_out, not_24_out, not_25_out, not_26_out, not_27_out, not_28_out,
       not_29_out, not_30_out, not_31_out, not_32_out, not_33_out, not_35_out, not_36_out, not_37_out,
       not_38_out, not_39_out, not_40_out, not_41_out, not_42_out, not_43_out, not_44_out, or_1_out,
       or_2_out, or_3_out, or_4_out, or_5_out, or_6_out;
  wire [3:0] CONSTANT_BUILDER_q, rom_1_data_2;
  wire [7:0] adder_1_out, nand_3_out, RA_q, RB_q;
  wire [7:4] CONSTANT_BUILDER_q_2, rom_1_data;
  wire [15:0] ADDR_q, B_LSB_q, counter_1_q;

  Register B_MSB (.D(out_5), .Q(B_LSB_q[15:8]), .clk(not_30_out), .clr(not_2_out));  // open: en
  Register B_LSB (.D(out_5), .Q(B_LSB_q[7:0]), .clk(not_29_out), .clr(not_2_out));  // open: en
  not not_1 (not_1_out, not_38_out);
  Counter #(.width(16), .max('hffff)) counter_1 (
    .load(not_4_out), .D(B_LSB_q), .count(not_28_out), .Q(counter_1_q), .clk(clock_1_out), .clr(not_2_out));  // open: carry
  not not_2 (not_2_out, CLEAR);
  Clock clock_1 (.out(clock_1_out));
  assign out_5 = not_1_out ? counter_1_q[15:8] : 8'bz;  // Controlled_Buffer controlled_buffer_1
  nand nand_1 (nand_1_out, ~not_3_out, not_39_out);  // NAND_Gate
  nand nand_2 (nand_2_out, not_3_out, not_39_out);
  not not_3 (not_3_out, not_31_out);
  Register #(.width(16)) ADDR (.D(B_LSB_q), .Q(ADDR_q), .clk(not_24_out));  // open: en, clr
  not not_4 (not_4_out, not_28_out);
  not not_5 (not_5_out, not_37_out);
  RAM #(.addrWidth(16), .bus("asynch")) ram_1 (
    .addr(B_LSB_q), .data(out_5), .sel(nand_1_out), .ld(nand_2_out), .clr(not_2_out));
  Decoder #(.select(3), .disabled(0)) decoder_1 (
    .out0(decoder_1_out0), .out1(decoder_1_out1), .out2(decoder_1_out2), .out3(decoder_1_out3),
    .out4(decoder_1_out4), .out5(decoder_1_out5), .out6(decoder_1_out6), .out7(decoder_1_out7),
    .sel(ADDR_q[15:13]), .en(not_6_out));
  not not_6 (not_6_out, not_35_out);
  ROM #(.addrWidth(15)) rom_1 (.addr(counter_1_q[15:1]), .data({rom_1_data, rom_1_data_2}));  // open: sel
  assign out_5 = not_5_out ? counter_1_q[7:0] : 8'bz;  // Controlled_Buffer controlled_buffer_2
  Register RA (.D(out_5), .Q(RA_q), .clk(not_32_out), .clr(not_2_out));  // open: en
  Register RB (.D(out_5), .Q(RB_q), .clk(not_33_out), .clr(not_2_out));  // open: en
  not not_7 (not_7_out, decoder_1_out0);
  // NOT_Gate not_8 has open pins: in=decoder_1_out1, out=open
  // NOT_Gate not_9 has open pins: in=decoder_1_out2, out=open
  // NOT_Gate not_10 has open pins: in=decoder_1_out3, out=open
  // NOT_Gate not_11 has open pins: in=decoder_1_out4, out=open
  // NOT_Gate not_12 has open pins: in=decoder_1_out5, out=open
  // NOT_Gate not_13 has open pins: in=decoder_1_out6, out=open
  // NOT_Gate not_14 has open pins: in=decoder_1_out7, out=open
  not not_15 (not_15_out, not_44_out);
  Adder adder_1 (.a(RA_q), .b(RB_q), .out(adder_1_out), .cin(not_40_out), .cout(adder_1_cout));
  assign nand_3_out = ~(RA_q & RB_q);  // NAND_Gate nand_3, 8 bits wide
  Comparator comparator_1 (.a(RA_q), .b(RB_q), .eq(comparator_1_eq));  // open: gt, lt
  nand nand_4 (nand_4_out, RB_q[0], RB_q[1], RB_q[2], RB_q[3], RB_q[4], RB_q[5], RB_q[6], RB_q[7]);
  Register register_1 (.D(out_5), .clk(not_7_out));  // open: en, Q, clr
  Register CONSTANT_BUILDER (
    .D({CONSTANT_BUILDER_q, rom_1_data_2}), .Q({CONSTANT_BUILDER_q_2, CONSTANT_BUILDER_q}), .clk(not_36_out),
    .clr(not_2_out));  // open: en
  assign out_5 = not_15_out ? {CONSTANT_BUILDER_q_2, CONSTANT_BUILDER_q} : 8'bz;  // Controlled_Buffer controlled_buffer_3
  not not_16 (not_16_out, and_1_out);
  assign out_5 = not_16_out ? adder_1_out : 8'bz;  // Controlled_Buffer controlled_buffer_4
  not not_17 (not_17_out, not_42_out);
  assign out_5 = not_17_out ? nand_3_out : 8'bz;  // Controlled_Buffer controlled_buffer_5
  and and_1 (and_1_out, not_41_out, not_40_out);
  not not_18 (not_18_out, comparator_1_eq);
  not not_19 (not_19_out, not_43_out);
  assign out_5 = not_19_out ? in_3 : 8'bz;  // Controlled_Buffer controlled_buffer_6
  nor nor_1 (nor_1_out, rom_1_data[7], rom_1_data_2[3]);
  not not_20 (not_20_out, decoder_2_out0);
  not not_21 (not_21_out, decoder_2_out1);
  not not_22 (not_22_out, decoder_2_out2);
  not not_23 (not_23_out, decoder_2_out3);
  not not_24 (not_24_out, decoder_2_out4);
  not not_25 (not_25_out, decoder_2_out5);
  not not_26 (not_26_out, decoder_2_out6);
  not not_27 (not_27_out, decoder_2_out7);
  Decoder #(.select(3), .disabled(0)) decoder_2 (
    .out0(decoder_2_out0), .out1(decoder_2_out1), .out2(decoder_2_out2), .out3(decoder_2_out3),
    .out4(decoder_2_out4), .out5(decoder_2_out5), .out6(decoder_2_out6), .out7(decoder_2_out7),
    .sel(rom_1_data[6:4]), .en(nor_1_out));
  or or_1 (or_1_out, not_26_out, EXTFLAGS[2]);
  or or_2 (or_2_out, EXTFLAGS[1], not_25_out);
  assign EXTDATA = not_43_out ? out_5 : 8'bz;  // Controlled_Buffer controlled_buffer_7
  or or_3 (or_3_out, not_22_out, adder_1_cout);
  or or_4 (or_4_out, not_23_out, RB_q[7]);
  nand nand_5 (nand_5_out, not_27_out, or_1_out, or_2_out, 1'b1, or_4_out, or_3_out, or_6_out, or_5_out);
  not not_28 (not_28_out, nand_5_out);
  or or_5 (or_5_out, not_20_out, not_18_out);
  or or_6 (or_6_out, not_21_out, nand_4_out);
  and and_2 (and_2_out, rom_1_data[7], counter_1_q[0]);
  Decoder #(.select(3), .disabled(0)) decoder_3 (
    .out0(decoder_3_out0), .out1(decoder_3_out1), .out2(decoder_3_out2), .out3(decoder_3_out3),
    .out4(decoder_3_out4), .out5(decoder_3_out5), .out6(decoder_3_out6), .out7(decoder_3_out7),
    .sel(rom_1_data[6:4]), .en(and_2_out));
  not not_29 (not_29_out, decoder_3_out0);
  not not_30 (not_30_out, decoder_3_out1);
  not not_31 (not_31_out, decoder_3_out2);
  not not_32 (not_32_out, decoder_3_out3);
  not not_33 (not_33_out, decoder_3_out4);
  // NOT_Gate not_34 has open pins: in=decoder_3_out5, out=open
  not not_35 (not_35_out, decoder_3_out6);
  not not_36 (not_36_out, decoder_3_out7);
  Decoder #(.select(4), .disabled(0)) decoder_4 (
    .out0(decoder_4_out0), .out1(decoder_4_out1), .out2(decoder_4_out2), .out3(decoder_4_out3),
    .out4(decoder_4_out4), .out5(decoder_4_out5), .out6(decoder_4_out6), .out7(decoder_4_out7),
    .out8(decoder_4_out8), .out9(decoder_4_out9), .out10(decoder_4_out10), .out11(decoder_4_out11),
    .out12(decoder_4_out12), .out13(decoder_4_out13), .out14(decoder_4_out14), .out15(decoder_4_out15),
    .sel(rom_1_data_2), .en(not_36_out));
  not not_37 (not_37_out, decoder_4_out0);
  not not_38 (not_38_out, decoder_4_out1);
  not not_39 (not_39_out, decoder_4_out2);
  not not_40 (not_40_out, decoder_4_out3);
  not not_41 (not_41_out, decoder_4_out4);
  not not_42 (not_42_out, decoder_4_out5);
  not not_43 (not_43_out, decoder_4_out6);
  not not_44 (not_44_out, decoder_4_out7);
  // NOT_Gate not_45 has open pins: in=decoder_4_out8, out=open
  // NOT_Gate not_46 has open pins: in=decoder_4_out9, out=open
  // NOT_Gate not_47 has open pins: in=decoder_4_out10, out=open
  // NOT_Gate not_48 has open pins: in=decoder_4_out11, out=open
  // NOT_Gate not_49 has open pins: in=decoder_4_out12, out=open
  // NOT_Gate not_50 has open pins: in=decoder_4_out13, out=open
  // NOT_Gate not_51 has open pins: in=decoder_4_out14, out=open
  // NOT_Gate not_52 has open pins: in=decoder_4_out15, out=open
  and and_3 (and_3_out, ~rom_1_data[7], rom_1_data_2[3]);  // AND_Gate
  Decoder #(.select(3), .disabled(0)) decoder_5 (
    .out0(decoder_5_out0), .out1(decoder_5_out1), .out2(decoder_5_out2), .out3(decoder_5_out3),
    .out4(decoder_5_out4), .out5(decoder_5_out5), .out6(decoder_5_out6), .out7(decoder_5_out7),
    .sel(rom_1_data_2[2:0]), .en(and_3_out));
  not not_53 (EXT_FLAGS[0], decoder_5_out0);
  not not_54 (EXT_FLAGS[1], decoder_5_out1);
  not not_55 (EXT_FLAGS[2], decoder_5_out2);
  not not_56 (EXT_FLAGS[3], decoder_5_out3);
  not not_57 (EXT_FLAGS[4], decoder_5_out4);
  not not_58 (EXT_FLAGS[5], decoder_5_out5);
  not not_59 (EXT_FLAGS[6], decoder_5_out6);
  not not_60 (EXT_FLAGS[7], decoder_5_out7);

  // Notes on the sheet:
  //   contents of rom_1 (hex, n*v repeats v):
  //   f0 0 e7 aa 3
  //   Bus Source Selector
  //   Bus driven by this selector
  //   except when RC is destination
endmodule
