// Logisim project 1b_serial_cpu.circ as structural Verilog: 1 circuit, main circuit main
module main (
);

  wire adder_1_cout, d_ff_1_q, nor_1_out, undriven, undriven_2;

  // NOR_Gate nor_1 has open pins: out=nor_1_out
  Adder #(.width(1)) adder_1 (.a(undriven), .b(nor_1_out), .cin(d_ff_1_q), .cout(adder_1_cout));  // open: out
  D_Flip_Flop d_ff_1 (.clk(undriven_2), .D(adder_1_cout), .Q(d_ff_1_q));  // open: Qn, preset, en, reset
endmodule
