// Logisim project 4b_cpu_rev1.circ as structural Verilog: 1 circuit, main circuit main
module main (
  input  [7:0] INPUT_DATA,
  input  in_2,
  output WRITE_ENABLE_N,
  output [3:0] OPA,
  output [3:0] OPB,
  output [3:0] RESULT,
  output [15:0] ADDR_OUTPUT
);

  wire adder_1_cout, clock_1_out, comparator_1_eq, multiplexer_2_out, not_1_out, not_2_out, not_3_out,
       not_4_out, not_5_out;
  wire [3:0] adder_1_out, nand_1_out;
  wire [7:7] counter_1_q, rom_1_data;
  wire [14:0] counter_1_q_2;

  Counter counter_1 (
    .Q({counter_1_q[7], counter_1_q_2[6:0]}), .clk(clock_1_out), .clr(in_2));  // open: load, D, count, carry
  Clock clock_1 (.out(clock_1_out));
  Counter counter_2 (
    .load(multiplexer_2_out), .D(ADDR_OUTPUT[7:0]), .Q(counter_1_q_2[14:7]), .clk(not_1_out), .clr(in_2));  // open: count, carry
  not not_1 (not_1_out, counter_1_q_2[6]);
  ROM #(.addrWidth(15)) rom_1 (.addr(counter_1_q_2), .data({rom_1_data[7], ADDR_OUTPUT[14:8]}));  // open: sel
  not not_2 (not_2_out, clock_1_out);
  not not_3 (not_3_out, rom_1_data[7]);
  not not_4 (not_4_out, ADDR_OUTPUT[12]);
  assign nand_1_out = ~(OPB & ADDR_OUTPUT[7:4]);  // NAND_Gate nand_1, 4 bits wide
  Adder #(.width(4)) adder_1 (
    .a(OPB), .b(ADDR_OUTPUT[7:4]), .out(adder_1_out), .cin(ADDR_OUTPUT[12]), .cout(adder_1_cout));
  RAM #(.addrWidth(2), .dataWidth(4), .bus("separate")) ram_1 (
    .addr(ADDR_OUTPUT[11:10]), .din(ADDR_OUTPUT[3:0]), .data(OPB), .str(not_3_out), .sel(not_4_out),
    .clk(not_2_out), .ld(1'b1), .clr(in_2));
  Multiplexer #(.select(2), .width(4), .enable("false")) multiplexer_1 (
    .in0(INPUT_DATA[3:0]), .in1(INPUT_DATA[7:4]), .in2(adder_1_out), .in3(nand_1_out), .out(RESULT),
    .sel(ADDR_OUTPUT[14:13]));
  Register register_1 (
    .D({ADDR_OUTPUT[3:0], RESULT}), .Q(ADDR_OUTPUT[7:0]), .clk(clock_1_out), .clr(in_2));  // open: en
  Pull_Resistor #(.pull(1)) pull_resistor_1 (.node(OPB));
  Comparator #(.width(4)) comparator_1 (.a(ADDR_OUTPUT[7:4]), .b(OPB), .eq(comparator_1_eq));  // open: gt, lt
  not not_5 (not_5_out, rom_1_data[7]);
  nand nand_2 (WRITE_ENABLE_N, ADDR_OUTPUT[12], not_5_out);
  Pull_Resistor pull_resistor_2 (.node(ADDR_OUTPUT[15]));
  Multiplexer #(.select(2), .disabled(0)) multiplexer_2 (
    .in0(1'b0), .in1(comparator_1_eq), .in2(adder_1_cout), .in3(1'b1), .out(multiplexer_2_out),
    .sel(ADDR_OUTPUT[9:8]), .en(clock_1_out));

  assign OPA = ADDR_OUTPUT[7:4];

  // Notes on the sheet:
  //   contents of rom_1 (hex, n*v repeats v):
  //   f0 40
endmodule
